// Logisim project EP2.circ as structural Verilog: 8 circuits, main circuit teste
module teste (
  input  in_1,
  input  in_2,
  input  in_3,
  input  in_4,
  output [15:0] out_5,
  output [15:0] out_6
);

  wire clock_1_out;
  wire [7:0] pc_1_output_address;
  wire [15:0] ram_1_data;

  Clock clock_1 (.out(clock_1_out));
  PC pc_1 (.Reset(in_1), .Counter_UP(clock_1_out), .Output_Address(pc_1_output_address));  // open: Set, Input_Address
  RAM #(.dataWidth(16)) ram_1 (
    .addr(pc_1_output_address), .data(ram_1_data), .sel(in_2), .ld(in_3), .clr(in_4));  // open: clk
  IR ir_1 (
    .\Código (ram_1_data[7:0]), .Set(clock_1_out), .\Endereço (ram_1_data[15:8]), .Output(out_5));  // open: Reset
  ACC acc_1 (.Input(ram_1_data), .Output(out_6), .Set(clock_1_out));  // open: Reset
endmodule

module PC (
  input  [7:0] Input_Address,
  input  Set,
  input  Reset,
  input  Counter_UP,
  output [7:0] Output_Address
);

  wire and_1_out, and_2_out, and_3_out, and_4_out, and_5_out, and_6_out, and_7_out, and_8_out, and_9_out,
       and_10_out, and_11_out, and_12_out, and_13_out, and_14_out, and_15_out, and_16_out, j_k_ff_1_qn,
       j_k_ff_2_qn, j_k_ff_3_qn, j_k_ff_4_qn, j_k_ff_5_qn, j_k_ff_6_qn, j_k_ff_7_qn, or_1_out, or_2_out,
       or_3_out, or_4_out, or_5_out, or_6_out, or_7_out, or_8_out;

  and and_1 (and_1_out, Set, Input_Address[0]);
  and and_2 (and_2_out, Set, ~Input_Address[0]);  // AND_Gate
  or or_1 (or_1_out, Reset, and_2_out);
  J_K_Flip_Flop j_k_ff_1 (
    .J(1'b1), .clk(Counter_UP), .K(1'b1), .Q(Output_Address[0]), .Qn(j_k_ff_1_qn), .preset(and_1_out),
    .en(1'b1), .reset(or_1_out));
  and and_3 (and_3_out, Set, Input_Address[2]);
  and and_4 (and_4_out, Set, Input_Address[1]);
  and and_5 (and_5_out, Set, ~Input_Address[1]);  // AND_Gate
  or or_2 (or_2_out, Reset, and_5_out);
  J_K_Flip_Flop j_k_ff_2 (
    .J(1'b1), .clk(j_k_ff_1_qn), .K(1'b1), .Q(Output_Address[1]), .Qn(j_k_ff_2_qn), .preset(and_4_out),
    .en(1'b1), .reset(or_2_out));
  and and_6 (and_6_out, Set, Input_Address[3]);
  and and_7 (and_7_out, Set, ~Input_Address[2]);  // AND_Gate
  or or_3 (or_3_out, Reset, and_7_out);
  J_K_Flip_Flop j_k_ff_3 (
    .J(1'b1), .clk(j_k_ff_2_qn), .K(1'b1), .Q(Output_Address[2]), .Qn(j_k_ff_3_qn), .preset(and_3_out),
    .en(1'b1), .reset(or_3_out));
  and and_8 (and_8_out, Set, Input_Address[4]);
  and and_9 (and_9_out, Set, ~Input_Address[3]);  // AND_Gate
  or or_4 (or_4_out, Reset, and_12_out);
  or or_5 (or_5_out, Reset, and_9_out);
  J_K_Flip_Flop j_k_ff_4 (
    .J(1'b1), .clk(j_k_ff_3_qn), .K(1'b1), .Q(Output_Address[3]), .Qn(j_k_ff_4_qn), .preset(and_6_out),
    .en(1'b1), .reset(or_5_out));
  and and_10 (and_10_out, Set, ~Input_Address[5]);  // AND_Gate
  and and_11 (and_11_out, Set, Input_Address[5]);
  and and_12 (and_12_out, Set, ~Input_Address[4]);  // AND_Gate
  or or_6 (or_6_out, Reset, and_10_out);
  and and_13 (and_13_out, Set, ~Input_Address[6]);  // AND_Gate
  and and_14 (and_14_out, Set, Input_Address[6]);
  or or_7 (or_7_out, Reset, and_13_out);
  J_K_Flip_Flop j_k_ff_5 (
    .J(1'b1), .clk(j_k_ff_4_qn), .K(1'b1), .Q(Output_Address[4]), .Qn(j_k_ff_5_qn), .preset(and_8_out),
    .en(1'b1), .reset(or_4_out));
  and and_15 (and_15_out, Set, Input_Address[7]);
  and and_16 (and_16_out, Set, ~Input_Address[7]);  // AND_Gate
  or or_8 (or_8_out, Reset, and_16_out);
  J_K_Flip_Flop j_k_ff_6 (
    .J(1'b1), .clk(j_k_ff_5_qn), .K(1'b1), .Q(Output_Address[5]), .Qn(j_k_ff_6_qn), .preset(and_11_out),
    .en(1'b1), .reset(or_6_out));
  J_K_Flip_Flop j_k_ff_7 (
    .J(1'b1), .clk(j_k_ff_6_qn), .K(1'b1), .Q(Output_Address[6]), .Qn(j_k_ff_7_qn), .preset(and_14_out),
    .en(1'b1), .reset(or_7_out));
  J_K_Flip_Flop j_k_ff_8 (
    .J(1'b1), .clk(j_k_ff_7_qn), .K(1'b1), .Q(Output_Address[7]), .preset(and_15_out), .en(1'b1),
    .reset(or_8_out));  // open: Qn
endmodule

module ACC (
  input  [15:0] Input,
  input  Set,
  input  Reset,
  output [15:0] Output
);

  Register #(.width(16)) register_1 (.D(Input), .en(1'b1), .Q(Output), .clk(Set), .clr(Reset));
endmodule

module IR (
  input  [7:0] \Código ,
  input  Set,
  input  Reset,
  input  [7:0] \Endereço ,
  output [15:0] Output
);

  Register register_1 (.D(\Código ), .en(1'b1), .Q(Output[7:0]), .clk(Set), .clr(Reset));
  Register register_2 (.D(\Endereço ), .en(1'b1), .Q(Output[15:8]), .clk(Set), .clr(Reset));
endmodule

module CTRL (
  input  [15:0] RAM_OUT,
  input  [7:0] PC_Address_OUT,
  input  [15:0] ACC_OUT,
  input  [15:0] IR_OUT,
  output RAM_CLR,
  output ACC_SET,
  output ACC_RESET,
  output Clock,
  output [15:0] ACC_IN,
  output PC_SET,
  output IR_SET,
  output PC_RESET,
  output IR_RESET,
  output [7:0] IR_Address,
  output [7:0] PC_Address_IN,
  output [7:0] IR_Codigo,
  output RAM_LD
);

  Clock clock_1 (.out(Clock));
  // Probe on nothing
  SPL168 spl168_1 (.in_1(IR_OUT), .out_2(IR_Address), .out_3(IR_Codigo));
  Comparator comparator_1 (.b(8'h33));  // open: a, gt, eq, lt
  Comparator comparator_2 (.a(IR_Address), .b(8'h33), .eq(ACC_SET));  // open: gt, lt
  Comparator comparator_3 (.b(8'h33));  // open: a, gt, eq, lt
  Comparator comparator_4 (.b(8'h33));  // open: a, gt, eq, lt
  Comparator comparator_5 (.b(8'h33));  // open: a, gt, eq, lt
endmodule

module teste2 (
  input  in_1,
  input  in_2,
  input  in_3,
  input  in_4,
  input  [7:0] in_5,
  input  in_6,
  input  in_7,
  input  in_8,
  input  [15:0] in_9,
  output [7:0] out_10,
  output [7:0] out_11,
  output [15:0] out_12
);

  wire ctrl_1_clock;
  wire [7:0] pc_1_output_address, spl168_1_out_2, spl168_1_out_3, spl168_2_out_3;
  wire [15:0] ram_1_data;

  CTRL ctrl_1 (
    .ACC_SET(in_2), .IR_Address(out_10), .IR_Codigo(out_11), .IR_OUT(out_12), .Clock(ctrl_1_clock));  // open: RAM_OUT, RAM_CLR, PC_SET, PC_RESET, PC_Address_IN, ACC_RESET, ACC_IN, IR_SET, IR_RESET, PC_Address_OUT, ACC_OUT, RAM_LD
  RAM #(.dataWidth(16)) ram_1 (
    .addr(pc_1_output_address), .data(ram_1_data), .sel(in_6), .clk(in_7), .ld(in_8));  // open: clr
  PC pc_1 (
    .Set(ctrl_1_clock), .Reset(in_3), .Counter_UP(ctrl_1_clock), .Input_Address(spl168_2_out_3),
    .Output_Address(pc_1_output_address));
  SPL168 spl168_1 (.in_1(ram_1_data), .out_2(spl168_1_out_2), .out_3(spl168_1_out_3));
  IR ir_1 (.\Código (spl168_1_out_3), .Set(ctrl_1_clock), .Reset(in_1), .\Endereço (spl168_1_out_2), .Output(out_12));
  SPL168 spl168_2 (.in_1(out_12), .out_3(spl168_2_out_3));  // open: out_2
  ACC acc_1 ();  // open: Input, Output, Set, Reset
endmodule

module SPL168 (
  input  [15:0] in_1,
  output [7:0] out_2,
  output [7:0] out_3
);


  assign out_2 = in_1[7:0];
  assign out_3 = in_1[15:8];
endmodule

module MRG816 (
  input  [7:0] in_1,
  input  [7:0] in_2,
  output [15:0] out_3
);


  assign out_3 = {in_2, in_1};
endmodule
